# Fritzing sketch TX1H_Tracker (saved by Fritzing 0.9.2b)

parts:
  U1 = attiny85 [package=dip]
  Part1 = Radiometrix NTX2
  LED1 = Billie the Blue LED
  LED2 = Gus the Green LED
  U2 = AVR 10-pin ICSP Header [package="avr icsp"]
  J$1 = SMA Antenna Connector [package=sma-edge]
  R1 = Resistor [tolerance=±5% resistance=220 package=THT]
  R2 = Resistor [tolerance=±5% resistance=220 package=THT]
  S1 = Toggle Switch [package=THT]

nets:
  N1: U1.Pin_1, U2.5
  N2: U1.Pin_2, Part1.TXD, R2.Pin_1
  N3: U1.Pin_3, Part1.En, R1.Pin_1
  N4: U1.Pin_4, Part1.0V, LED1.cathode, LED2.cathode, U2.10, S1.COM
  N5: U1.Pin_5, U2.1
  N6: U1.Pin_6, U2.9
  N7: U1.Pin_7, U2.7, S1.L1
  N8: U1.Pin_8, Part1.Vcc, U2.2
  N9: Part1.RF_out, J$1.SIGNAL
  N10: Part1.RF_gnd, J$1.GND
  N11: LED1.anode, R2.Pin_0
  N12: LED2.anode, R1.Pin_0

custom parts:
  Radiometrix NTX2: The NTX2 transmitter and NRX2 receiver offer a low power, reliable data link in a Radiometrix SIL standard pin out and foot print.
